# Fritzing sketch lizard (saved by Fritzing 0.9.2b)
breadboards: 1

parts:
  Bauteil1 = Arduino Uno (Rev3)
  S1 = Pushbutton [package="[THT]"]
  R1 = Resistor [tolerance=±5% resistance=220 package=THT]
  U1 = RELAY [package=relay-jzc]  # not connected

nets:
  N1: Bauteil1.D11_PWM/MOSI, S1.Pin_4, R1.Pin_0
  N2: Bauteil1.5V, S1.Pin_2
  N3: Bauteil1.GND, R1.Pin_1
